// Logisim project Delphi.Jr.circ as structural Verilog: 6 circuits, main circuit Delphi.Jr
module Delphi_Jr (
  input  ready,
  input  [19:0] input_to_RAM,
  input  [7:0] Imm8,
  input  [3:0] op_code,
  input  reboot__h_w_button,
  input  [19:0] in_6,
  input  mode__h_w_button,
  output Overflow,
  output Carry
);

  wire arithmetic_logical_unit_alu_1_greater_than_gf, arithmetic_logical_unit_alu_1_less_than_lf,
       arithmetic_logical_unit_alu_1_zero_zf, bus_splitter_1_jump_enable, bus_splitter_1_mem_flush,
       bus_splitter_1_mem_write_control, bus_splitter_1_mov_instr, bus_splitter_1_write_enable_mem,
       bus_splitter_1_write_type, demultiplexer_1_out0, demultiplexer_1_out1, flag_store_1_gf_o,
       flag_store_1_lf_o, flag_store_1_zf_o, multiplexer_5_out;
  wire [1:0] bus_splitter_1_alu_o2_typeselect, bus_splitter_1_clock_control, bus_splitter_1_decision_make,
       bus_splitter_1_o1_regselect, bus_splitter_1_o2_regselect, bus_splitter_1_type_o1,
       bus_splitter_1_type_o2, multiplexer_1_out, multiplexer_2_out, not_1_out, not_2_out;
  wire [3:0] control_unit_cu_1__4_bit_opcodel;
  wire [7:0] arithmetic_logical_unit_alu_1_output_o1, arithmetic_logical_unit_alu_1_output_o2,
       bit_extender_2_out, control_unit_cu_1__8_bit_operand, controlled_buffer_1_out, memory_unit_mu_1_o1,
       memory_unit_mu_1_o2, multiplexer_3_out, multiplexer_4_out, multiplexer_7_out;
  wire [19:0] bit_extender_1_out, control_unit_cu_1__20_bit_control_signal, demultiplexer_2_out0,
       demultiplexer_2_out1, memory_unit_mu_1__20_bit_stored_value, multiplexer_6_out;

  assign not_1_out = ~2'b10;  // NOT_Gate not_1, 2 bits wide
  Multiplexer #(.width(2)) multiplexer_1 (
    .in0(not_1_out), .in1(2'b10), .out(multiplexer_1_out), .sel(ready));  // open: en
  Multiplexer #(.width(2)) multiplexer_2 (
    .in0(multiplexer_1_out), .in1(not_2_out), .out(multiplexer_2_out), .sel(mode__h_w_button));  // open: en
  Multiplexer #(.width(8)) multiplexer_3 (
    .in0(arithmetic_logical_unit_alu_1_output_o1), .in1(control_unit_cu_1__8_bit_operand),
    .out(multiplexer_3_out), .sel(bus_splitter_1_mov_instr));  // open: en
  Multiplexer #(.width(8)) multiplexer_4 (
    .in0(arithmetic_logical_unit_alu_1_output_o2), .in1(control_unit_cu_1__8_bit_operand),
    .out(multiplexer_4_out), .sel(bus_splitter_1_mov_instr));  // open: en
  Demultiplexer demultiplexer_1 (
    .out0(demultiplexer_1_out0), .out1(demultiplexer_1_out1), .in(multiplexer_5_out),
    .sel(bus_splitter_1_jump_enable));  // open: en
  Multiplexer #(.select(2)) multiplexer_5 (
    .in0(1'b1), .in1(flag_store_1_zf_o), .in2(flag_store_1_gf_o), .in3(flag_store_1_lf_o),
    .out(multiplexer_5_out), .sel(bus_splitter_1_decision_make));  // open: en
  Memory_Unit__MU memory_unit_mu_1 (
    .O1_register_select(bus_splitter_1_o1_regselect), .Input_Data_1(multiplexer_3_out),
    .O2_register_select(bus_splitter_1_o2_regselect), .type_O1(bus_splitter_1_type_o1),
    .Input_data_2(multiplexer_4_out), .type_O2(bus_splitter_1_type_o2), .Write_to_RAM(multiplexer_6_out),
    .Write_type(bus_splitter_1_write_type), .write_enable_mem(bus_splitter_1_write_enable_mem),
    .execute(mode__h_w_button), .clock_controller(multiplexer_2_out),
    .write_enable_reg(demultiplexer_1_out0), .mem_cum_stack_pointer_reset(bus_splitter_1_mem_flush),
    .reg_flush(reboot__h_w_button), .O1(memory_unit_mu_1_o1), .O2(memory_unit_mu_1_o2),
    ._20_bit_stored_value(memory_unit_mu_1__20_bit_stored_value), .jump_enable(demultiplexer_1_out1),
    .mode(reboot__h_w_button), .jump_address(controlled_buffer_1_out));
  assign controlled_buffer_1_out = demultiplexer_1_out1 ? control_unit_cu_1__8_bit_operand : 8'bz;  // Controlled_Buffer controlled_buffer_1
  Multiplexer #(.width(20)) multiplexer_6 (
    .in0(input_to_RAM), .in1(bit_extender_1_out), .out(multiplexer_6_out),
    .sel(bus_splitter_1_mem_write_control));  // open: en
  assign bit_extender_1_out = {{12{memory_unit_mu_1_o1[7]}}, memory_unit_mu_1_o1};  // Bit_Extender bit_extender_1
  flag_store flag_store_1 (
    .ZF(arithmetic_logical_unit_alu_1_zero_zf), .GF(arithmetic_logical_unit_alu_1_greater_than_gf),
    .LF(arithmetic_logical_unit_alu_1_less_than_lf), .ZF_O(flag_store_1_zf_o), .GF_O(flag_store_1_gf_o),
    .LF_O(flag_store_1_lf_o));
  Demultiplexer #(.width(20)) demultiplexer_2 (
    .out0(demultiplexer_2_out0), .out1(demultiplexer_2_out1), .in(memory_unit_mu_1__20_bit_stored_value),
    .sel(mode__h_w_button));  // open: en
  Multiplexer #(.select(2), .width(8)) multiplexer_7 (
    .in1(memory_unit_mu_1_o2), .in2(bit_extender_2_out), .in3(control_unit_cu_1__8_bit_operand),
    .out(multiplexer_7_out), .sel(bus_splitter_1_alu_o2_typeselect));  // open: in0, en
  Bit_Extender #(.in_width(20), .out_width(8)) bit_extender_2 (.in(demultiplexer_2_out0), .out(bit_extender_2_out));
  Arithmetic_Logical_Unit__ALU arithmetic_logical_unit_alu_1 (
    .O1_input_8_bit(memory_unit_mu_1_o1), .O2_input_8_bit(multiplexer_7_out),
    .Opcode_4_bit(control_unit_cu_1__4_bit_opcodel), .Carry_CF(Carry), .Overflow_OF(Overflow),
    .greater_than_GF(arithmetic_logical_unit_alu_1_greater_than_gf),
    .Zero_ZF(arithmetic_logical_unit_alu_1_zero_zf),
    .less_than_LF(arithmetic_logical_unit_alu_1_less_than_lf),
    .Output_O1(arithmetic_logical_unit_alu_1_output_o1), .Output_O2(arithmetic_logical_unit_alu_1_output_o2));
  Control_Unit__CU control_unit_cu_1 (
    .imm_20_bit_control_signal(in_6), .imm_4_bit_opcode(op_code), .imm_8_bit_operand(Imm8),
    .toggle_operation_mode(mode__h_w_button),
    ._20_bit_control_signal(control_unit_cu_1__20_bit_control_signal),
    ._20_bit_instruction_from_RAM(demultiplexer_2_out1), ._8_bit_operand(control_unit_cu_1__8_bit_operand),
    ._4_bit_opcodel(control_unit_cu_1__4_bit_opcodel));
  assign not_2_out = ~bus_splitter_1_clock_control;  // NOT_Gate not_2, 2 bits wide
  // Probe on memory_unit_mu_1_o1
  // Probe on demultiplexer_2_out1
  bus_splitter bus_splitter_1 (
    .type_O1(bus_splitter_1_type_o1), .type_O2(bus_splitter_1_type_o2),
    .O1_regselect(bus_splitter_1_o1_regselect), .O2_regselect(bus_splitter_1_o2_regselect),
    .ALU_O2_typeselect(bus_splitter_1_alu_o2_typeselect), .decision_make(bus_splitter_1_decision_make),
    .clock_control(bus_splitter_1_clock_control),
    ._20_bit_control_signal(control_unit_cu_1__20_bit_control_signal),
    .mem_write_control(bus_splitter_1_mem_write_control), .mem_flush(bus_splitter_1_mem_flush),
    .mov_instr(bus_splitter_1_mov_instr), .jump_enable(bus_splitter_1_jump_enable),
    .Write_enable_mem(bus_splitter_1_write_enable_mem), .Write_type(bus_splitter_1_write_type));
  // Probe on memory_unit_mu_1_o2

  // Notes on the sheet:
  //   *write the program while ready is in '0'.
  //   controlsignal
  //   Output-probes
  //   control-instruction(RAM)
endmodule

module Memory_Unit__MU (
  input  [1:0] O1_register_select,
  input  [7:0] Input_Data_1,
  input  [1:0] O2_register_select,
  input  [1:0] type_O1,
  input  write_enable_reg,
  input  reg_flush,
  input  [7:0] Input_data_2,
  input  [1:0] type_O2,
  input  execute,
  input  mem_cum_stack_pointer_reset,
  input  [19:0] Write_to_RAM,
  input  Write_type,
  input  jump_enable,
  input  mode,
  input  [7:0] jump_address,
  input  [1:0] clock_controller,
  input  write_enable_mem,
  output [7:0] O1,
  output [7:0] O2,
  output [19:0] _20_bit_stored_value
);

  wire clock_1_out, demultiplexer_2_out1, demultiplexer_2_out2, demultiplexer_2_out3, demultiplexer_3_out1,
       demultiplexer_3_out2, demultiplexer_3_out3, demultiplexer_5_out0, demultiplexer_5_out1,
       demultiplexer_5_out2, demultiplexer_5_out3, demultiplexer_6_out0, demultiplexer_6_out1,
       demultiplexer_6_out2, demultiplexer_6_out3, multiplexer_1_out, not_2_out, not_3_out;
  wire [7:0] adder_1_out, controlled_buffer_1_out, controlled_buffer_2_out, controlled_buffer_5_out,
       controlled_buffer_7_out, controlled_buffer_8_out, controlled_buffer_11_out, controlled_buffer_13_out,
       demultiplexer_1_out1, demultiplexer_1_out2, demultiplexer_1_out3, demultiplexer_4_out1,
       demultiplexer_4_out2, demultiplexer_4_out3, demultiplexer_7_out0, demultiplexer_7_out1,
       demultiplexer_7_out2, demultiplexer_7_out3, demultiplexer_8_out0, demultiplexer_8_out1,
       demultiplexer_8_out2, demultiplexer_8_out3, multiplexer_2_out, multiplexer_3_out, multiplexer_4_out,
       multiplexer_5_out, multiplexer_6_out, multiplexer_7_out, not_1_out, register_1_q, register_2_q,
       register_3_q, register_4_q, register_5_q, register_6_q;

  Demultiplexer #(.select(2), .width(8)) demultiplexer_1 (
    .out1(demultiplexer_1_out1), .out2(demultiplexer_1_out2), .out3(demultiplexer_1_out3), .in(Input_Data_1),
    .sel(type_O1));  // open: out0, en
  Demultiplexer #(.select(2)) demultiplexer_2 (
    .out1(demultiplexer_2_out1), .out2(demultiplexer_2_out2), .out3(demultiplexer_2_out3), .in(1'b1),
    .sel(type_O1));  // open: out0, en
  Demultiplexer #(.select(2)) demultiplexer_3 (
    .out1(demultiplexer_3_out1), .out2(demultiplexer_3_out2), .out3(demultiplexer_3_out3), .in(1'b1),
    .sel(type_O2));  // open: out0, en
  Demultiplexer #(.select(2), .width(8)) demultiplexer_4 (
    .out1(demultiplexer_4_out1), .out2(demultiplexer_4_out2), .out3(demultiplexer_4_out3), .in(Input_data_2),
    .sel(type_O2));  // open: out0, en
  Clock clock_1 (.out(clock_1_out));
  assign controlled_buffer_1_out = demultiplexer_2_out1 ? demultiplexer_1_out1 : 8'bz;  // Controlled_Buffer controlled_buffer_1
  assign controlled_buffer_2_out = demultiplexer_2_out3 ? demultiplexer_1_out3 : 8'bz;  // Controlled_Buffer controlled_buffer_2
  assign controlled_buffer_2_out = demultiplexer_3_out3 ? demultiplexer_4_out3 : 8'bz;  // Controlled_Buffer controlled_buffer_3
  assign controlled_buffer_1_out = demultiplexer_3_out1 ? demultiplexer_4_out1 : 8'bz;  // Controlled_Buffer controlled_buffer_4
  assign controlled_buffer_5_out = demultiplexer_2_out2 ? demultiplexer_1_out2 : 8'bz;  // Controlled_Buffer controlled_buffer_5
  Multiplexer #(.select(2)) multiplexer_1 (
    .in0(clock_1_out), .in1(1'b1), .in2(1'b0), .in3(clock_1_out), .out(multiplexer_1_out),
    .sel(clock_controller));  // open: en
  assign controlled_buffer_5_out = demultiplexer_3_out2 ? demultiplexer_4_out2 : 8'bz;  // Controlled_Buffer controlled_buffer_6
  Multiplexer #(.width(8)) multiplexer_2 (
    .in0(controlled_buffer_2_out), .in1(register_2_q), .out(multiplexer_2_out), .sel(execute));  // open: en
  assign not_1_out = ~multiplexer_5_out;  // NOT_Gate not_1, 8 bits wide
  Register register_1 (.D(not_1_out), .en(1'b1), .Q(register_1_q), .clk(multiplexer_1_out), .clr(mode));
  Demultiplexer #(.select(2)) demultiplexer_5 (
    .out0(demultiplexer_5_out0), .out1(demultiplexer_5_out1), .out2(demultiplexer_5_out2),
    .out3(demultiplexer_5_out3), .in(1'b1), .sel(O1_register_select));  // open: en
  Demultiplexer #(.select(2)) demultiplexer_6 (
    .out0(demultiplexer_6_out0), .out1(demultiplexer_6_out1), .out2(demultiplexer_6_out2),
    .out3(demultiplexer_6_out3), .in(1'b1), .sel(O2_register_select));  // open: en
  Multiplexer #(.width(8)) multiplexer_3 (
    .in0(multiplexer_2_out), .in1(multiplexer_4_out), .out(multiplexer_3_out), .sel(write_enable_mem));  // open: en
  Multiplexer #(.width(8)) multiplexer_4 (
    .in0(register_1_q), .in1(register_2_q), .out(multiplexer_4_out), .sel(Write_type));  // open: en
  Register register_2 (.D(multiplexer_5_out), .en(1'b1), .Q(register_2_q), .clk(multiplexer_1_out), .clr(mode));
  Multiplexer #(.width(8)) multiplexer_5 (
    .in0(adder_1_out), .in1(jump_address), .out(multiplexer_5_out), .sel(jump_enable));  // open: en
  Adder adder_1 (.a(register_2_q), .b(8'h1), .out(adder_1_out));  // open: cin, cout
  Demultiplexer #(.select(2), .width(8)) demultiplexer_7 (
    .out0(demultiplexer_7_out0), .out1(demultiplexer_7_out1), .out2(demultiplexer_7_out2),
    .out3(demultiplexer_7_out3), .in(controlled_buffer_1_out), .sel(O1_register_select));  // open: en
  Demultiplexer #(.select(2), .width(8)) demultiplexer_8 (
    .out0(demultiplexer_8_out0), .out1(demultiplexer_8_out1), .out2(demultiplexer_8_out2),
    .out3(demultiplexer_8_out3), .in(controlled_buffer_5_out), .sel(O2_register_select));  // open: en
  not not_2 (not_2_out, multiplexer_1_out);
  assign controlled_buffer_7_out = demultiplexer_6_out1 ? demultiplexer_8_out1 : 8'bz;  // Controlled_Buffer controlled_buffer_7
  assign controlled_buffer_8_out = demultiplexer_5_out0 ? demultiplexer_7_out0 : 8'bz;  // Controlled_Buffer controlled_buffer_8
  assign controlled_buffer_8_out = demultiplexer_6_out0 ? demultiplexer_8_out0 : 8'bz;  // Controlled_Buffer controlled_buffer_9
  assign controlled_buffer_7_out = demultiplexer_5_out1 ? demultiplexer_7_out1 : 8'bz;  // Controlled_Buffer controlled_buffer_10
  assign controlled_buffer_11_out = demultiplexer_5_out2 ? demultiplexer_7_out2 : 8'bz;  // Controlled_Buffer controlled_buffer_11
  assign controlled_buffer_11_out = demultiplexer_6_out2 ? demultiplexer_8_out2 : 8'bz;  // Controlled_Buffer controlled_buffer_12
  assign controlled_buffer_13_out = demultiplexer_6_out3 ? demultiplexer_8_out3 : 8'bz;  // Controlled_Buffer controlled_buffer_13
  assign controlled_buffer_13_out = demultiplexer_5_out3 ? demultiplexer_7_out3 : 8'bz;  // Controlled_Buffer controlled_buffer_14
  not not_3 (not_3_out, write_enable_mem);
  Register register_3 (
    .D(controlled_buffer_8_out), .en(write_enable_reg), .Q(register_3_q), .clk(not_2_out), .clr(reg_flush));
  Register register_4 (
    .D(controlled_buffer_7_out), .en(write_enable_reg), .Q(register_4_q), .clk(not_2_out), .clr(reg_flush));
  Register register_5 (
    .D(controlled_buffer_11_out), .en(write_enable_reg), .Q(register_5_q), .clk(not_2_out), .clr(reg_flush));
  Register register_6 (
    .D(controlled_buffer_13_out), .en(write_enable_reg), .Q(register_6_q), .clk(not_2_out), .clr(reg_flush));
  RAM #(.dataWidth(20), .bus("separate")) ram_1 (
    .addr(multiplexer_3_out), .din(Write_to_RAM), .data(_20_bit_stored_value), .str(write_enable_mem),
    .sel(1'b1), .clk(multiplexer_1_out), .ld(not_3_out), .clr(mem_cum_stack_pointer_reset));
  Multiplexer #(.select(2), .width(8)) multiplexer_6 (
    .in0(register_3_q), .in1(register_4_q), .in2(register_5_q), .in3(register_6_q), .out(multiplexer_6_out),
    .sel(O1_register_select));  // open: en
  Multiplexer #(.select(2), .width(8)) multiplexer_7 (
    .in0(register_3_q), .in1(register_4_q), .in2(register_5_q), .in3(register_6_q), .out(multiplexer_7_out),
    .sel(O2_register_select));  // open: en
  Multiplexer #(.select(2), .width(8)) multiplexer_8 (
    .in1(multiplexer_6_out), .in2(multiplexer_7_out), .out(O1), .sel(type_O1));  // open: in0, in3, en
  Multiplexer #(.select(2), .width(8)) multiplexer_9 (
    .in1(multiplexer_6_out), .in2(multiplexer_7_out), .out(O2), .sel(type_O2));  // open: in0, in3, en

  // Notes on the sheet:
  //   Write Enable(Ram)
  //   Operand -1 (8-bit)
  //   (INPUT)
  //   Operand -2 (8-bit)
  //   (INPUT)
  //   Operand-1
  //   Operand -2
  //   store 
  //   ('0' to load, store otherwise,)
  //   clock
  //   write enable.(0 to disable writes)
  //   select
  //   Clock
  //   flush the memory
  //   flush registers to '0' if '1'
  //   (OUTPUT)
  //   (OUTPUT)
endmodule

module Arithmetic_Logical_Unit__ALU (
  input  [7:0] O1_input_8_bit,
  input  [7:0] O2_input_8_bit,
  input  [3:0] Opcode_4_bit,
  output greater_than_GF,
  output Zero_ZF,
  output less_than_LF,
  output Carry_CF,
  output Overflow_OF,
  output [7:0] Output_O1,
  output [7:0] Output_O2
);

  wire comparator_1_eq, or_2_out, or_3_out, or_4_out;
  wire [2:0] bit_extender_1_out, bit_extender_2_out, bit_extender_3_out, bit_extender_4_out,
       bit_extender_5_out;
  wire [3:0] xnor_1_out;
  wire [7:0] adder_1_out, and_1_out, demultiplexer_1_out1, demultiplexer_1_out2, demultiplexer_1_out3,
       demultiplexer_1_out4, demultiplexer_1_out5, demultiplexer_1_out6, demultiplexer_1_out7,
       demultiplexer_1_out8, demultiplexer_1_out9, demultiplexer_1_out10, demultiplexer_1_out11,
       demultiplexer_1_out12, demultiplexer_1_out13, demultiplexer_1_out14, demultiplexer_2_out1,
       demultiplexer_2_out2, demultiplexer_2_out3, demultiplexer_2_out4, demultiplexer_2_out5,
       demultiplexer_2_out6, demultiplexer_2_out7, demultiplexer_2_out8, demultiplexer_2_out9,
       demultiplexer_2_out10, demultiplexer_2_out11, demultiplexer_2_out12, demultiplexer_2_out13,
       demultiplexer_2_out14, divider_1_out, divider_1_rem, multiplier_1_cout, multiplier_1_out, not_1_out,
       not_2_out, or_1_out, shifter_1_out, shifter_2_out, shifter_3_out, shifter_4_out, shifter_5_out,
       subtractor_1_out, xor_1_out;

  Shifter #(.shift("rr")) shifter_1 (.in(demultiplexer_1_out10), .\dist (bit_extender_2_out), .out(shifter_1_out));
  Bit_Extender #(.out_width(3)) bit_extender_1 (.in(demultiplexer_2_out9), .out(bit_extender_1_out));
  Shifter #(.shift("rl")) shifter_2 (.in(demultiplexer_1_out9), .\dist (bit_extender_1_out), .out(shifter_2_out));
  assign not_1_out = ~demultiplexer_1_out14;  // NOT_Gate not_1, 8 bits wide
  Shifter #(.shift("lr")) shifter_3 (.in(demultiplexer_1_out7), .\dist (bit_extender_3_out), .out(shifter_3_out));
  assign xor_1_out = demultiplexer_1_out13 ^ demultiplexer_2_out13;  // XOR_Gate xor_1, 8 bits wide
  Multiplexer #(.select(4), .width(8)) multiplexer_1 (
    .in1(adder_1_out), .in2(subtractor_1_out), .in3(multiplier_1_out), .in4(divider_1_out),
    .in6(shifter_5_out), .in7(shifter_3_out), .in8(shifter_4_out), .in9(shifter_2_out), .in10(shifter_1_out),
    .in11(and_1_out), .in12(or_1_out), .in13(xor_1_out), .in14(not_1_out), .out(Output_O1), .sel(Opcode_4_bit));  // open: in0, in5, in15, en
  Bit_Extender #(.out_width(3)) bit_extender_2 (.in(demultiplexer_2_out10), .out(bit_extender_2_out));
  Bit_Extender #(.out_width(3)) bit_extender_3 (.in(demultiplexer_2_out7), .out(bit_extender_3_out));
  Multiplier multiplier_1 (
    .a(demultiplexer_1_out3), .b(demultiplexer_2_out3), .out(multiplier_1_out), .cout(multiplier_1_cout));  // open: cin
  Divider divider_1 (
    .a(demultiplexer_1_out4), .b(demultiplexer_2_out4), .out(divider_1_out), .rem(divider_1_rem));  // open: upper
  Demultiplexer #(.select(4), .width(8)) demultiplexer_1 (
    .out1(demultiplexer_1_out1), .out2(demultiplexer_1_out2), .out3(demultiplexer_1_out3),
    .out4(demultiplexer_1_out4), .out5(demultiplexer_1_out5), .out6(demultiplexer_1_out6),
    .out7(demultiplexer_1_out7), .out8(demultiplexer_1_out8), .out9(demultiplexer_1_out9),
    .out10(demultiplexer_1_out10), .out11(demultiplexer_1_out11), .out12(demultiplexer_1_out12),
    .out13(demultiplexer_1_out13), .out14(demultiplexer_1_out14), .in(O1_input_8_bit), .sel(Opcode_4_bit));  // open: out0, out15, en
  assign or_1_out = demultiplexer_1_out12 | demultiplexer_2_out12;  // OR_Gate or_1, 8 bits wide
  Adder adder_1 (.a(demultiplexer_1_out1), .b(demultiplexer_2_out1), .out(adder_1_out), .cout(Carry_CF));  // open: cin
  Demultiplexer #(.select(4), .width(8)) demultiplexer_2 (
    .out1(demultiplexer_2_out1), .out2(demultiplexer_2_out2), .out3(demultiplexer_2_out3),
    .out4(demultiplexer_2_out4), .out5(demultiplexer_2_out5), .out6(demultiplexer_2_out6),
    .out7(demultiplexer_2_out7), .out8(demultiplexer_2_out8), .out9(demultiplexer_2_out9),
    .out10(demultiplexer_2_out10), .out11(demultiplexer_2_out11), .out12(demultiplexer_2_out12),
    .out13(demultiplexer_2_out13), .out14(demultiplexer_2_out14), .in(O2_input_8_bit), .sel(Opcode_4_bit));  // open: out0, out15, en
  Subtractor subtractor_1 (
    .a(demultiplexer_1_out2), .b(demultiplexer_2_out2), .out(subtractor_1_out), .bout(Overflow_OF));  // open: bin
  Multiplexer #(.select(4), .width(8)) multiplexer_2 (
    .in3(multiplier_1_cout), .in4(divider_1_rem), .in14(not_2_out), .out(Output_O2), .sel(Opcode_4_bit));  // open: in0, in1, in2, in5, in6, in7, in8, in9, in10, in11, in12, in13, in15, en
  Bit_Extender #(.out_width(3)) bit_extender_4 (.in(demultiplexer_2_out6), .out(bit_extender_4_out));
  assign xnor_1_out = ~(4'b1010 ^ Opcode_4_bit);  // XNOR_Gate xnor_1, 4 bits wide
  Bit_Extender #(.out_width(3)) bit_extender_5 (.in(demultiplexer_2_out8), .out(bit_extender_5_out));
  Shifter #(.shift("ar")) shifter_4 (.in(demultiplexer_1_out8), .\dist (bit_extender_5_out), .out(shifter_4_out));
  Comparator comparator_1 (
    .a(demultiplexer_1_out5), .b(demultiplexer_2_out5), .gt(greater_than_GF), .eq(comparator_1_eq),
    .lt(less_than_LF));
  Shifter shifter_5 (.in(demultiplexer_1_out6), .\dist (bit_extender_4_out), .out(shifter_5_out));
  Multiplexer multiplexer_3 (.in0(comparator_1_eq), .in1(1'b0), .out(Zero_ZF), .sel(or_3_out));  // open: en
  or or_2 (or_2_out, xnor_1_out[0], xnor_1_out[1]);
  or or_3 (or_3_out, or_2_out, or_4_out);
  or or_4 (or_4_out, xnor_1_out[2], xnor_1_out[3]);
  assign and_1_out = demultiplexer_1_out11 & demultiplexer_2_out11;  // AND_Gate and_1, 8 bits wide
  assign not_2_out = ~demultiplexer_2_out14;  // NOT_Gate not_2, 8 bits wide
endmodule

module Control_Unit__CU (
  input  [19:0] imm_20_bit_control_signal,
  input  [3:0] imm_4_bit_opcode,
  input  [7:0] imm_8_bit_operand,
  input  toggle_operation_mode,
  input  [19:0] _20_bit_instruction_from_RAM,
  output [7:0] _8_bit_operand,
  output [19:0] _20_bit_control_signal,
  output [3:0] _4_bit_opcodel
);

  wire clock_1_out;
  wire [3:0] multiplexer_2_out;
  wire [7:0] multiplexer_3_out;
  wire [19:0] multiplexer_1_out, rom_1_data;

  Clock clock_1 (.out(clock_1_out));
  Multiplexer #(.width(20)) multiplexer_1 (
    .in0(imm_20_bit_control_signal), .in1(rom_1_data), .out(multiplexer_1_out), .sel(toggle_operation_mode));  // open: en
  Register #(.width(20)) register_1 (
    .D(multiplexer_1_out), .en(1'b1), .Q(_20_bit_control_signal), .clk(clock_1_out));  // open: clr
  Multiplexer #(.width(4)) multiplexer_2 (
    .in0(imm_4_bit_opcode), .in1(_20_bit_instruction_from_RAM[11:8]), .out(multiplexer_2_out),
    .sel(toggle_operation_mode));  // open: en
  Register #(.width(4)) register_2 (
    .D(multiplexer_2_out), .en(1'b1), .Q(_4_bit_opcodel), .clk(clock_1_out));  // open: clr
  Register register_3 (.D(multiplexer_3_out), .en(1'b1), .Q(_8_bit_operand), .clk(clock_1_out));  // open: clr
  ROM #(.dataWidth(20)) rom_1 (.addr(_20_bit_instruction_from_RAM[19:12]), .data(rom_1_data), .sel(1'b1));
  Multiplexer #(.width(8)) multiplexer_3 (
    .in0(imm_8_bit_operand), .in1(_20_bit_instruction_from_RAM[7:0]), .out(multiplexer_3_out),
    .sel(toggle_operation_mode));  // open: en

  // Notes on the sheet:
  //   contents of rom_1 (hex, n*v repeats v):
  //   80 15*0 614c0 624c0 634c0 644c0 664c0 674c0 684c0 694c0 6b4c0 6c4c0 6d4c0 6e4c0 708c0 748c0 788c0
  //   7c8c0 400c4 440c4 480c4 4c0c4 12*0 400d1 500d1 600d1 700d1 12*0 1c0 2c0 3c0 13*0 d8 15*0 1d8 15*0
  //   2d8 15*0 3d8
endmodule

module bus_splitter (
  input  [19:0] _20_bit_control_signal,
  output mem_write_control,
  output mem_flush,
  output [1:0] type_O1,
  output mov_instr,
  output [1:0] type_O2,
  output jump_enable,
  output Write_enable_mem,
  output [1:0] O1_regselect,
  output Write_type,
  output [1:0] O2_regselect,
  output [1:0] ALU_O2_typeselect,
  output [1:0] decision_make,
  output [1:0] clock_control
);


  assign ALU_O2_typeselect = _20_bit_control_signal[11:10];
  assign clock_control = _20_bit_control_signal[7:6];
  assign decision_make = _20_bit_control_signal[9:8];
  assign jump_enable = _20_bit_control_signal[3];
  assign mem_flush = _20_bit_control_signal[1];
  assign mem_write_control = _20_bit_control_signal[0];
  assign mov_instr = _20_bit_control_signal[2];
  assign O1_regselect = _20_bit_control_signal[15:14];
  assign O2_regselect = _20_bit_control_signal[13:12];
  assign type_O1 = _20_bit_control_signal[19:18];
  assign type_O2 = _20_bit_control_signal[17:16];
  assign Write_enable_mem = _20_bit_control_signal[4];
  assign Write_type = _20_bit_control_signal[5];
endmodule

module flag_store (
  input  ZF,
  input  GF,
  input  LF,
  output ZF_O,
  output GF_O,
  output LF_O
);

  wire clock_1_out;

  Clock clock_1 (.out(clock_1_out));
  Register #(.width(1), .trigger("falling")) register_1 (.D(ZF), .en(1'b1), .Q(ZF_O), .clk(clock_1_out));  // open: clr
  Register #(.width(1), .trigger("falling")) register_2 (.D(GF), .en(1'b1), .Q(GF_O), .clk(clock_1_out));  // open: clr
  Register #(.width(1), .trigger("falling")) register_3 (.D(LF), .en(1'b1), .Q(LF_O), .clk(clock_1_out));  // open: clr
endmodule
